// Logisim project 7_Seg_Driver.circ as structural Verilog: 9 circuits, main circuit main
module main (
  input  B3,
  input  B2,
  input  B1,
  input  B0
);

  wire n7_seg_driver_1_a, n7_seg_driver_1_b, n7_seg_driver_1_c, n7_seg_driver_1_d, n7_seg_driver_1_e,
       n7_seg_driver_1_f, n7_seg_driver_1_g;

  _7_seg_Driver u_7_seg_driver_1 (
    .a(n7_seg_driver_1_a), .b(n7_seg_driver_1_b), .c(n7_seg_driver_1_c), .d(n7_seg_driver_1_d),
    .e(n7_seg_driver_1_e), .f(n7_seg_driver_1_f), .g(n7_seg_driver_1_g), .B0(B0), .B1(B1), .B2(B2), .B3(B3));
  _7_Segment_Display u_7_segment_display_1 (
    .g(n7_seg_driver_1_g), .f(n7_seg_driver_1_f), .a(n7_seg_driver_1_a), .b(n7_seg_driver_1_b),
    .e(n7_seg_driver_1_e), .d(n7_seg_driver_1_d), .c(n7_seg_driver_1_c));  // open: dp
endmodule

// s_A
module seg_A (
  input  b0,
  input  b1,
  input  b2,
  input  b3,
  output a
);

  wire and_1_out, and_2_out, and_3_out, and_4_out, and_5_out, and_6_out, not_1_out, not_2_out, not_3_out,
       not_4_out, not_5_out, not_6_out, not_7_out;

  not not_1 (not_1_out, b1);
  and and_1 (and_1_out, not_1_out, not_2_out);
  not not_2 (not_2_out, b3);
  not not_3 (not_3_out, b0);
  and and_2 (and_2_out, not_3_out, b2);
  not not_4 (not_4_out, b0);
  and and_3 (and_3_out, not_4_out, b1, b3);
  and and_4 (and_4_out, b1, b2);
  not not_5 (not_5_out, b1);
  and and_5 (and_5_out, b0, not_5_out, not_6_out);
  not not_6 (not_6_out, b2);
  and and_6 (and_6_out, b0, not_7_out);
  not not_7 (not_7_out, b3);
  or or_1 (a, and_1_out, and_2_out, and_3_out, and_4_out, and_5_out, and_6_out);
endmodule

// s_B
module seg_B (
  input  b0,
  input  b1,
  input  b2,
  input  b3,
  output b
);

  wire and_1_out, and_2_out, and_3_out, and_4_out, and_5_out, and_6_out, not_1_out, not_2_out, not_3_out,
       not_4_out, not_5_out, not_6_out, not_7_out, not_8_out, not_9_out, not_10_out, not_11_out;

  not not_1 (not_1_out, b0);
  and and_1 (and_1_out, not_1_out, not_2_out);
  not not_2 (not_2_out, b1);
  not not_3 (not_3_out, b0);
  not not_4 (not_4_out, b2);
  and and_2 (and_2_out, not_3_out, not_4_out, not_5_out);
  not not_5 (not_5_out, b3);
  not not_6 (not_6_out, b1);
  and and_3 (and_3_out, not_6_out, not_7_out);
  not not_7 (not_7_out, b2);
  not not_8 (not_8_out, b1);
  and and_4 (and_4_out, not_8_out, not_9_out);
  not not_9 (not_9_out, b3);
  not not_10 (not_10_out, b0);
  and and_5 (and_5_out, not_10_out, b2, b3);
  not not_11 (not_11_out, b2);
  and and_6 (and_6_out, b0, not_11_out, b3);
  or or_1 (b, and_1_out, and_2_out, and_3_out, and_4_out, and_5_out, and_6_out);
endmodule

// s_C
module seg_C (
  input  b0,
  input  b1,
  input  b2,
  input  b3,
  output c
);

  wire and_1_out, and_2_out, and_3_out, and_4_out, and_5_out, not_1_out, not_2_out, not_3_out, not_4_out,
       not_5_out, not_6_out;

  not not_1 (not_1_out, b0);
  and and_1 (and_1_out, not_1_out, not_2_out);
  not not_2 (not_2_out, b2);
  not not_3 (not_3_out, b0);
  and and_2 (and_2_out, not_3_out, b3);
  not not_4 (not_4_out, b2);
  and and_3 (and_3_out, not_4_out, b3);
  not not_5 (not_5_out, b0);
  and and_4 (and_4_out, not_5_out, b1);
  and and_5 (and_5_out, b0, not_6_out);
  not not_6 (not_6_out, b1);
  or or_1 (c, and_1_out, and_2_out, and_3_out, and_4_out, and_5_out);
endmodule

// s_D
module seg_D (
  input  b0,
  input  b1,
  input  b2,
  input  b3,
  output d
);

  wire and_1_out, and_2_out, and_3_out, and_4_out, and_5_out, not_1_out, not_2_out, not_3_out, not_4_out,
       not_5_out, not_6_out, not_7_out;

  not not_1 (not_1_out, b0);
  and and_1 (and_1_out, not_1_out, not_2_out, not_3_out);
  not not_2 (not_2_out, b1);
  not not_3 (not_3_out, b3);
  not not_4 (not_4_out, b1);
  and and_2 (and_2_out, not_4_out, b2, b3);
  not not_5 (not_5_out, b2);
  and and_3 (and_3_out, b1, not_5_out, b3);
  and and_4 (and_4_out, b1, b2, not_6_out);
  not not_6 (not_6_out, b3);
  and and_5 (and_5_out, b0, not_7_out);
  not not_7 (not_7_out, b2);
  or or_1 (d, and_1_out, and_2_out, and_3_out, and_4_out, and_5_out);
endmodule

// s_E
module seg_E (
  input  b0,
  input  b1,
  input  b2,
  input  b3,
  output e
);

  wire and_1_out, and_2_out, and_3_out, and_4_out, not_1_out, not_2_out, not_3_out;

  not not_1 (not_1_out, b1);
  and and_1 (and_1_out, not_1_out, not_2_out);
  not not_2 (not_2_out, b3);
  and and_2 (and_2_out, b2, not_3_out);
  not not_3 (not_3_out, b3);
  and and_3 (and_3_out, b0, b2);
  and and_4 (and_4_out, b0, b1);
  or or_1 (e, and_1_out, and_2_out, and_3_out, and_4_out);
endmodule

// s_F
module seg_F (
  input  b0,
  input  b1,
  input  b2,
  input  b3,
  output f
);

  wire and_1_out, and_2_out, and_3_out, and_4_out, and_5_out, not_1_out, not_2_out, not_3_out, not_4_out,
       not_5_out, not_6_out;

  not not_1 (not_1_out, b2);
  and and_1 (and_1_out, not_1_out, not_2_out);
  not not_2 (not_2_out, b3);
  not not_3 (not_3_out, b0);
  and and_2 (and_2_out, not_3_out, b1, not_4_out);
  not not_4 (not_4_out, b2);
  and and_3 (and_3_out, b1, not_5_out);
  not not_5 (not_5_out, b3);
  and and_4 (and_4_out, b0, not_6_out);
  not not_6 (not_6_out, b1);
  and and_5 (and_5_out, b0, b2);
  or or_1 (f, and_1_out, and_2_out, and_3_out, and_4_out, and_5_out);
endmodule

// s_G
module seg_G (
  input  b0,
  input  b1,
  input  b2,
  input  b3,
  output g
);

  wire and_1_out, and_2_out, and_3_out, and_4_out, and_5_out, not_1_out, not_2_out, not_3_out, not_4_out,
       not_5_out;

  not not_1 (not_1_out, b1);
  and and_1 (and_1_out, not_1_out, b2);
  and and_2 (and_2_out, b2, not_2_out);
  not not_2 (not_2_out, b3);
  not not_3 (not_3_out, b0);
  and and_3 (and_3_out, not_3_out, b1, not_4_out);
  not not_4 (not_4_out, b2);
  and and_4 (and_4_out, b0, not_5_out);
  not not_5 (not_5_out, b1);
  and and_5 (and_5_out, b0, b3);
  or or_1 (g, and_1_out, and_2_out, and_3_out, and_4_out, and_5_out);
endmodule

// 7_Seg_Driver
module _7_seg_Driver (
  input  B0,
  input  B1,
  input  B2,
  input  B3,
  output a,
  output b,
  output c,
  output d,
  output e,
  output f,
  output g
);

  seg_A seg_a_1 (.b0(B3), .b1(B2), .b2(B1), .b3(B0), .a(a));
  seg_B seg_b_1 (.b0(B3), .b1(B2), .b2(B1), .b3(B0), .b(b));
  seg_C seg_c_1 (.b0(B3), .b1(B2), .b2(B1), .b3(B0), .c(c));
  seg_D seg_d_1 (.b0(B3), .b1(B2), .b2(B1), .b3(B0), .d(d));
  seg_E seg_e_1 (.b0(B3), .b1(B2), .b2(B1), .b3(B0), .e(e));
  seg_F seg_f_1 (.b0(B3), .b1(B2), .b2(B1), .b3(B0), .f(f));
  seg_G seg_g_1 (.b0(B3), .b1(B2), .b2(B1), .b3(B0), .g(g));
endmodule
