// Logisim project Memory_game.circ as structural Verilog: 2 circuits, main circuit main
module main (
  input  En
);

  wire and_1_out, and_2_out, and_3_out, and_4_out, and_5_out, and_6_out, and_7_out, BUTON_1_q, BUTON_2_q,
       BUTON_3_q, BUTON_4_q, BUTON_5_q, button_1_out, clock_1_out, n4_bit_counter_1_b0, n4_bit_counter_1_b1,
       n4_bit_counter_1_b2, n4_bit_counter_1_b3, n4_bit_counter_1_co, n7_seg_driver_1_a, n7_seg_driver_1_b,
       n7_seg_driver_1_c, n7_seg_driver_1_d, n7_seg_driver_1_e, n7_seg_driver_1_f, n7_seg_driver_1_g,
       random_1_out, random_2_out, random_3_out, random_4_out, random_5_out, xnor_1_out, xnor_2_out,
       xnor_3_out, xnor_4_out, xnor_5_out;

  Clock clock_1 (.out(clock_1_out));
  Random #(.width(1)) random_1 (.clk(clock_1_out), .next(clock_1_out), .out(random_1_out));  // open: clr
  Random #(.width(1)) random_2 (.clk(clock_1_out), .next(clock_1_out), .out(random_2_out));  // open: clr
  Random #(.width(1)) random_3 (.clk(clock_1_out), .next(clock_1_out), .out(random_3_out));  // open: clr
  Random #(.width(1)) random_4 (.clk(clock_1_out), .next(clock_1_out), .out(random_4_out));  // open: clr
  Random #(.width(1)) random_5 (.clk(clock_1_out), .next(clock_1_out), .out(random_5_out));  // open: clr
  LED led_1 (.in(and_1_out));
  and and_1 (and_1_out, random_1_out, clock_1_out);
  and and_2 (and_2_out, random_2_out, clock_1_out);
  LED led_2 (.in(and_2_out));
  and and_3 (and_3_out, random_3_out, clock_1_out);
  LED led_3 (.in(and_3_out));
  LED led_4 (.in(and_4_out));
  and and_4 (and_4_out, random_4_out, clock_1_out);
  and and_5 (and_5_out, random_5_out, clock_1_out);
  LED led_5 (.in(and_5_out));
  LED led_6 (.in(BUTON_1_q));
  LED led_7 (.in(BUTON_2_q));
  LED led_8 (.in(BUTON_3_q));
  LED led_9 (.in(BUTON_4_q));
  LED led_10 (.in(BUTON_5_q));
  Button button_1 (.out(button_1_out));
  J_K_Flip_Flop BUTON_1 (.Q(BUTON_1_q));  // open: J, clk, K, Qn, preset, en, reset
  J_K_Flip_Flop BUTON_2 (.Q(BUTON_2_q));  // open: J, clk, K, Qn, preset, en, reset
  J_K_Flip_Flop BUTON_3 (.Q(BUTON_3_q));  // open: J, clk, K, Qn, preset, en, reset
  J_K_Flip_Flop BUTON_4 (.Q(BUTON_4_q));  // open: J, clk, K, Qn, preset, en, reset
  J_K_Flip_Flop BUTON_5 (.Q(BUTON_5_q));  // open: J, clk, K, Qn, preset, en, reset
  xnor xnor_1 (xnor_1_out, BUTON_1_q, random_1_out);
  xnor xnor_2 (xnor_2_out, BUTON_2_q, random_2_out);
  xnor xnor_3 (xnor_3_out, BUTON_3_q, random_3_out);
  xnor xnor_4 (xnor_4_out, BUTON_4_q, random_4_out);
  xnor xnor_5 (xnor_5_out, BUTON_5_q, random_5_out);
  and and_6 (and_6_out, xnor_1_out, xnor_2_out, xnor_3_out, xnor_4_out, xnor_5_out);
  and and_7 (and_7_out, and_6_out, button_1_out);
  _4_Bit_Counter u_4_bit_counter_1 (
    .Enable(En), .Clk(and_7_out), .B0(n4_bit_counter_1_b0), .B1(n4_bit_counter_1_b1),
    .B2(n4_bit_counter_1_b2), .B3(n4_bit_counter_1_b3), .Co(n4_bit_counter_1_co));
  LED led_11 (.in(n4_bit_counter_1_co));
  _7_seg_Driver u_7_seg_driver_1 (
    .a(n7_seg_driver_1_a), .b(n7_seg_driver_1_b), .c(n7_seg_driver_1_c), .d(n7_seg_driver_1_d),
    .e(n7_seg_driver_1_e), .f(n7_seg_driver_1_f), .g(n7_seg_driver_1_g), .B0(n4_bit_counter_1_b0),
    .B1(n4_bit_counter_1_b1), .B2(n4_bit_counter_1_b2), .B3(n4_bit_counter_1_b3));
  _7_Segment_Display u_7_segment_display_1 (
    .g(n7_seg_driver_1_g), .f(n7_seg_driver_1_f), .a(n7_seg_driver_1_a), .b(n7_seg_driver_1_b),
    .e(n7_seg_driver_1_e), .d(n7_seg_driver_1_d), .c(n7_seg_driver_1_c));  // open: dp

  // Notes on the sheet:
  //   FII ATENT !
  //   RASPUNS FINAL
  //   BUTOANE
  //   Co
  //   RASPUNSURI CORECTE 0-16
endmodule

module _4_Bit_Counter (
  input  Enable,
  input  Clk,
  output B0,
  output B1,
  output B2,
  output B3,
  output Co
);

  wire and_1_out, and_2_out, and_3_out;

  and and_1 (and_1_out, Enable, B0);
  and and_2 (and_2_out, and_1_out, B1);
  and and_3 (and_3_out, and_2_out, B2);
  J_K_Flip_Flop j_k_ff_1 (.J(Enable), .clk(Clk), .K(Enable), .Q(B0));  // open: Qn, preset, en, reset
  J_K_Flip_Flop j_k_ff_2 (.J(and_1_out), .clk(Clk), .K(and_1_out), .Q(B1));  // open: Qn, preset, en, reset
  J_K_Flip_Flop j_k_ff_3 (.J(and_2_out), .clk(Clk), .K(and_2_out), .Q(B2));  // open: Qn, preset, en, reset
  J_K_Flip_Flop j_k_ff_4 (.J(and_3_out), .clk(Clk), .K(and_3_out), .Q(B3));  // open: Qn, preset, en, reset
  and and_4 (Co, B3, and_3_out);
endmodule
